# Fritzing sketch schematic (saved by Fritzing 1.0.5)
breadboards: 1

parts:
  1_Arduino_Vin_->_18650_x_2 = Arduino Uno (Rev3) - ICSP
  7_4V_18650_x_2_Li-ion_battery_/_BMS = L298N DC motor driver
  5v_regulated_output = DC Motor [voltage_(max)=6V voltage_(min)=3V]
  2_servo_->_5V_regulated_output_(L298N) = HC-SR04 Ultrasonic Distance Sensor
  L298N_5V_output_is_sufficient_for_this_single_servo_project = Pushbutton [package="[THT]"]
  LED1 = smd LED [color="Red (633nm)" package="1206 [SMD]"]
  common_GND = DC Motor [voltage_(max)=6V voltage_(min)=3V]
  R1 = Resistor [tolerance=±5% resistance=330 package="2512 [SMD]"]
  R2 = Photocell (LDR) [power=0.25W dark_resistance_@0.01lx=300kΩ light_resistance_@100lx=400Ω luminance=10lx package=THT]
  R3 = Photocell (LDR) [power=0.25W dark_resistance_@0.01lx=300kΩ light_resistance_@100lx=400Ω luminance=10lx package=THT]
  R4 = Photocell (LDR) [power=0.25W dark_resistance_@0.01lx=300kΩ light_resistance_@100lx=400Ω luminance=10lx package=THT]
  R5 = Resistor [tolerance=±5% resistance=10k package="2512 [SMD]"]
  R6 = Resistor [tolerance=±5% resistance=10k package="2512 [SMD]"]
  R7 = Resistor [tolerance=±5% resistance=10k package="2512 [SMD]"]
  VCC1 = Battery [internal_resistance=0.1Ω]
  3_Note_A_seperate_5V_regulator_could_be_used_but_the = Basic Servo
  J1 = Piezo Speaker

nets:
  N1: 1_Arduino_Vin_->_18650_x_2.A0, 1_Arduino_Vin_->_18650_x_2.5V, R2.pin_1, R3.pin_0, R4.pin_0, R4.pin_1, R5.Pin_0
  N2: 1_Arduino_Vin_->_18650_x_2.A1, R2.pin_0, R6.Pin_0
  N3: 1_Arduino_Vin_->_18650_x_2.A2, R3.pin_1, R7.Pin_1
  N4: 1_Arduino_Vin_->_18650_x_2.ICSP_MISO, 1_Arduino_Vin_->_18650_x_2.D12/MISO, J1.pin2
  N5: 1_Arduino_Vin_->_18650_x_2.ICSP_SCK, 1_Arduino_Vin_->_18650_x_2.D13/SCK, LED1.anode
  N6: 1_Arduino_Vin_->_18650_x_2.ICSP_MOSI, 1_Arduino_Vin_->_18650_x_2.D11_PWM/MOSI, 3_Note_A_seperate_5V_regulator_could_be_used_but_the.pulse
  N7: 1_Arduino_Vin_->_18650_x_2.GND, L298N_5V_output_is_sufficient_for_this_single_servo_project.Pin_1, L298N_5V_output_is_sufficient_for_this_single_servo_project.Pin_2, R1.Pin_1, R5.Pin_1, R6.Pin_1, R7.Pin_0, J1.pin1
  N8: 1_Arduino_Vin_->_18650_x_2.D8, 7_4V_18650_x_2_Li-ion_battery_/_BMS.IN3
  N9: 1_Arduino_Vin_->_18650_x_2.D9_PWM, 7_4V_18650_x_2_Li-ion_battery_/_BMS.IN2
  N10: 1_Arduino_Vin_->_18650_x_2.D10_PWM/SS, 7_4V_18650_x_2_Li-ion_battery_/_BMS.IN1
  N11: 1_Arduino_Vin_->_18650_x_2.D2, L298N_5V_output_is_sufficient_for_this_single_servo_project.Pin_3, L298N_5V_output_is_sufficient_for_this_single_servo_project.Pin_4
  N12: 1_Arduino_Vin_->_18650_x_2.D3_PWM, 2_servo_->_5V_regulated_output_(L298N).TRIG
  N13: 1_Arduino_Vin_->_18650_x_2.D4, 2_servo_->_5V_regulated_output_(L298N).ECHO
  N14: 1_Arduino_Vin_->_18650_x_2.D5_PWM, 7_4V_18650_x_2_Li-ion_battery_/_BMS.ENA
  N15: 1_Arduino_Vin_->_18650_x_2.D6_PWM, 7_4V_18650_x_2_Li-ion_battery_/_BMS.ENB
  N16: 1_Arduino_Vin_->_18650_x_2.D7, 7_4V_18650_x_2_Li-ion_battery_/_BMS.IN4
  N17: 7_4V_18650_x_2_Li-ion_battery_/_BMS.OUT1, 5v_regulated_output.pin_2
  N18: 7_4V_18650_x_2_Li-ion_battery_/_BMS.OUT2, 5v_regulated_output.pin_1
  N19: 7_4V_18650_x_2_Li-ion_battery_/_BMS.OUT3, common_GND.pin_2
  N20: 7_4V_18650_x_2_Li-ion_battery_/_BMS.OUT4, common_GND.pin_1
  N21: 7_4V_18650_x_2_Li-ion_battery_/_BMS.12V, VCC1.+
  N22: 7_4V_18650_x_2_Li-ion_battery_/_BMS.GND, VCC1.-
  VCC: 2_servo_->_5V_regulated_output_(L298N).VCC, 3_Note_A_seperate_5V_regulator_could_be_used_but_the.vcc
  GND: 2_servo_->_5V_regulated_output_(L298N).GND, 3_Note_A_seperate_5V_regulator_could_be_used_but_the.gnd

custom parts:
  L298N DC motor driver: 2x DC motor driver with 78M05 positive voltage regulator (7..35 V) L298N: max 46 V, 2 A Set 5 V Enable jumper to enable 5 V regultor (needed for the L298N) and +5 V output at screw terminal or supply external +5 V at screw terminal Set ENA and/or ENB to +5 V to enable motor permanently or supply ENA and/or ENB with PWM signal IN1 and IN2 set rotation directory for motor A (OUT1/OUT2) IN2 and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
